# Fritzing sketch batteryTester (saved by Fritzing 0.9.3b)
breadboards: 1

parts:
  부품1 = Arduino Uno (Rev3)  # not connected
  U1 = BATTERY-2 [package=battery-aa]
  부품2 = Zeta LCD keypad shield for Arduino

nets:
  N1: U1.-1, 부품2.GND
  N2: U1.+1, 부품2.A1

custom parts:
  Zeta LCD keypad shield for Arduino: The LCD shield for Arduino
